// Digital circuit misa.dig as structural Verilog
module misa (
  input  clk
);

  wire alu__cout, alu__n, alu__v, alu__z, and_1_out, and_2_out, and_3_out, and_4_out, and_5_out,
       comparator_1_eq, comparator_2_eq, comparator_3_eq, comparator_4_eq, ctl__add, ctl__mem__rdinst,
       ctl__mem__read, ctl__mem__wrback, ctl__mem__write, ctl__negb, ctl__op__adc, ctl__op__add,
       ctl__op__and, ctl__op__halt, ctl__op__jal, ctl__op__jmp, ctl__op__lw, ctl__op__or, ctl__op__rcc,
       ctl__op__rsr, ctl__op__sbb, ctl__op__set, ctl__op__sub, ctl__op__sw, ctl__op__wsr, ctl__op__xor,
       ctl__port1__write, ctl__use__imm, ctl__use__port1, ctl__use__port2, ctl__use__port3, ctl__wrflags,
       jk_ff_2_nq, or_1_out, stage__execute, stage__fetch, stage__fetchhi, stage__fetchlo;
  wire [1:0] stage;
  wire [3:0] decoder_1_dec__csr, decoder_1_dec__op, decoder_1_dec__rd, decoder_1_dec__rs1,
       decoder_1_dec__rs2, multiplexer_1_out, multiplexer_2_out, multiplexer_4_out;
  wire [7:0] alu__b, alu__y, decoder_1_dec__imm, demultiplexer_1_out_0, demultiplexer_1_out_1,
       mem__read__data, reg__port1__data_in, reg__port1__data_out, reg__port2__data_out, reg__port3__data;
  wire [15:0] add_1_s, csrfile_1_csr__flags__out, inst, mem__addr, multiplexer_3_out, multiplexer_6_out, pc;

  Comparator #(.Bits(4)) comparator_1 (.a(decoder_1_dec__csr), .b(4'b0001), .eq(comparator_1_eq));  // open: gt, lt
  Comparator #(.Bits(4)) comparator_2 (.a(decoder_1_dec__csr), .b(4'b0010), .eq(comparator_2_eq));  // open: gt, lt
  Comparator #(.Bits(4)) comparator_3 (.a(decoder_1_dec__csr), .b(4'b0011), .eq(comparator_3_eq));  // open: gt, lt
  Comparator #(.Bits(4)) comparator_4 (.a(decoder_1_dec__csr), .b(4'b0100), .eq(comparator_4_eq));  // open: gt, lt
  and and_1 (and_1_out, comparator_1_eq, ctl__op__wsr);
  and and_2 (and_2_out, comparator_2_eq, ctl__op__wsr);
  and and_3 (and_3_out, comparator_4_eq, ctl__op__wsr);
  and and_4 (and_4_out, ctl__wrflags, comparator_3_eq);
  and and_5 (and_5_out, comparator_3_eq, ctl__op__wsr);
  or or_1 (or_1_out, and_4_out, and_5_out);
  Multiplexer #(.Bits(4)) multiplexer_1 (
    .sel(ctl__use__port3), .in_0(4'b0000), .in_1(decoder_1_dec__rs2), .out(multiplexer_1_out));
  decoder decoder_1 (
    .dec__inst(inst), .dec__op(decoder_1_dec__op), .dec__rd(decoder_1_dec__rd),
    .dec__rs1(decoder_1_dec__rs1), .dec__rs2(decoder_1_dec__rs2), .dec__imm(decoder_1_dec__imm),
    .dec__csr(decoder_1_dec__csr));  // open: dec__cmp
  Multiplexer #(.Bits(4)) multiplexer_2 (
    .sel(ctl__use__port2), .in_0(4'b0000), .in_1(decoder_1_dec__rs1), .out(multiplexer_2_out));
  Multiplexer #(.Bits(16)) multiplexer_3 (
    .sel(ctl__wrflags), .in_0({reg__port1__data_out, reg__port2__data_out}),
    .in_1({{12{1'b0}}, alu__v, alu__n, alu__cout, alu__z}), .out(multiplexer_3_out));
  Multiplexer #(.Bits(4)) multiplexer_4 (
    .sel(ctl__use__port1), .in_0(4'b0000), .in_1(decoder_1_dec__rd), .out(multiplexer_4_out));
  regfile regfile_1 (
    .reg__port1(multiplexer_4_out), .reg__port2(multiplexer_2_out), .reg__port3(multiplexer_1_out),
    .reg__port1__write(ctl__port1__write), .reg__port2__write(1'b0), .reg__clk(clk),
    .reg__port1__data(reg__port1__data_out), .reg__port2__data(reg__port2__data_out),
    .reg__port3__data(reg__port3__data));
  csrfile csrfile_1 (
    .csr__saddr__in({reg__port1__data_out, reg__port2__data_out}),
    .csr__raddr__in({reg__port1__data_out, reg__port2__data_out}), .csr__flags__in(multiplexer_3_out),
    .csr__cause__in({reg__port1__data_out, reg__port2__data_out}), .csr__saddr__write(and_1_out),
    .csr__raddr__write(and_2_out), .csr__flags__write(or_1_out), .csr__cause__write(and_3_out),
    .csr__clk(clk), .csr__flags__out(csrfile_1_csr__flags__out));  // open: csr__saddr__out, csr__raddr__out, csr__cause__out, csr__extns__out
  // control control_1: pin names not known; wires that end beside it: stage, decoder_1_dec__op, ctl__op__halt, ctl__op__add, ctl__op__adc, ctl__op__sub, ctl__op__sbb, ctl__op__and, ctl__op__or, ctl__op__xor, ctl__op__rcc, ctl__op__set, ctl__op__lw, ctl__op__sw, ctl__op__rsr, ctl__op__wsr, ctl__op__jal, ctl__op__jmp, ctl__port1__write, ctl__negb, ctl__add, ctl__mem__wrback, ctl__mem__rdinst, ctl__mem__read
  assign reg__port1__data_out = ctl__port1__write ? reg__port1__data_in : 8'bz;  // Driver driver_1
  // comparator comparator_5: pin names not known; wires that end beside it: csrfile_1_csr__flags__out
  Multiplexer #(.Bits(8)) multiplexer_5 (
    .sel(ctl__use__imm), .in_0(reg__port3__data), .in_1(decoder_1_dec__imm), .out(alu__b));
  Register #(.Bits(16)) register_1 (.D(add_1_s), .C(clk), .en(1'b1), .Q(pc));
  JK_FF jk_ff_1 (.J(jk_ff_2_nq), .C(clk), .K(1'b1), .Q(stage[0]));  // open: nQ
  arithmetic arithmetic_1 (
    .alu__a(reg__port2__data_out), .alu__b(alu__b), .alu__negb(ctl__negb), .alu__and(ctl__op__and),
    .alu__or(ctl__op__or), .alu__xor(ctl__op__xor), .alu__rot(ctl__op__rcc), .alu__cin(ctl__op__sub),
    .alu__add(ctl__add), .alu__y(alu__y), .alu__z(alu__z), .alu__cout(alu__cout), .alu__n(alu__n),
    .alu__v(alu__v));
  Multiplexer #(.Bits(16)) multiplexer_6 (.sel(stage__fetch), .in_0({16{1'b0}}), .in_1(16'h1), .out(multiplexer_6_out));
  JK_FF jk_ff_2 (.J(stage[0]), .C(clk), .K(1'b1), .Q(stage[1]), .nQ(jk_ff_2_nq));
  Demultiplexer #(.Selector_Bits(2), .Bits(8)) demultiplexer_1 (
    .sel(stage), .in(mem__read__data), .out_0(demultiplexer_1_out_0), .out_1(demultiplexer_1_out_1));  // open: out_2, out_3
  Add #(.Bits(16)) add_1 (.a(pc), .b(multiplexer_6_out), .c_i(1'b0), .s(add_1_s));  // open: c_o
  Register #(.Bits(8)) register_2 (.D(demultiplexer_1_out_0), .C(clk), .en(stage__fetchlo), .Q(inst[7:0]));
  Register #(.Bits(8)) register_3 (.D(demultiplexer_1_out_1), .C(clk), .en(stage__fetchhi), .Q(inst[15:8]));
  Demultiplexer #(.Selector_Bits(2)) demultiplexer_2 (
    .sel(stage), .in(1'b1), .out_0(stage__fetchlo), .out_1(stage__fetchhi), .out_2(stage__execute));  // open: out_3
  or or_2 (stage__fetch, stage__fetchhi, stage__fetchlo);
  Multiplexer #(.Bits(8)) multiplexer_7 (
    .sel(ctl__mem__wrback), .in_0(alu__y), .in_1(mem__read__data), .out(reg__port1__data_in));
  Multiplexer #(.Bits(16)) multiplexer_8 (
    .sel(ctl__mem__rdinst), .in_0({reg__port2__data_out, reg__port3__data}), .in_1(pc), .out(mem__addr));
  memory memory_1 (
    .mem__write__data(reg__port1__data_out), .mem__addr(mem__addr), .mem__read(ctl__mem__read),
    .mem__write(ctl__mem__write), .mem__clk(clk), .mem__read__data(mem__read__data));  // open: mem__ready

  // Notes on the sheet:
  //   clk: Hz: 10
  //   ALU B generation
  //   Clock
  //   Progress:
  //   ADD - Done
  //   ADC - Need cin logic
  //   SUB - Need cin logic
  //   SBB - Need cin logic
  //   AND - Done
  //   OR   - Done
  //   XOR - Done
  //   RCC - Need cin logic
  //   SET - Done
  //   LW  - Done
  //   SW  - Done
  //   RSR - Need csr file
  //   WSR - Need csr file
  //   JAL - Need branch logic
  //   JMP - Need branch logic
  //   Program counter
  //   Stage counter
  //   Instruction register
  //   Reg writeback generation
  //   Memory address generation
  //   Stage signals
endmodule
